# Fritzing sketch Feather_M0Lora_Maxbotix (saved by Fritzing 0.9.3b)

parts:
  U1 = LIPO-1000mAh [package=lipo-1000]  # not connected
  SONAR1 = Maxbotix MaxSonar Ultrasonic Sensor (Hi-Res)
  Part12 = Adafruit Feather M0 RFM9x LoRa [part_number="Adafruit #3178 or #3179"]

nets:
  GND: SONAR1.GND, Part12.GND
  N1: SONAR1.+5V, Part12.VBAT
  N2: SONAR1.RX, Part12.D6
  N3: SONAR1.PW, Part12.D5

custom parts:
  Maxbotix MaxSonar Ultrasonic Sensor (Hi-Res): Maxbotix MaxSonar Hi-Resolution Ultrasonic Sensor HRLV-EZ0, HRLV-EZ1, HRLV-EZ2, HRLV-EZ3, HRLV-EZ4
  Adafruit Feather M0 RFM9x LoRa: This is the Adafruit Feather M0 RFM95 LoRa Radio - our take on an microcontroller with a "Long Range (LoRa)" packet radio transceiver with built in USB and battery charging. Its an Adafruit Feather M0 with a 433Mhz or 900MHz radio module cooked in! Great for making wireless networks that are more flexible than Bluetooth LE and without the high power requirements of WiFi. We have other boards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
