# Fritzing sketch Feather_M0_Maxbotix (saved by Fritzing 0.9.3b)

parts:
  Part11 = Adafruit Feather M0 Basic Proto [part_number="Adafruit #2772"]
  U1 = LIPO-1000mAh [package=lipo-1000]  # not connected
  SONAR1 = Maxbotix MaxSonar Ultrasonic Sensor (Hi-Res)

nets:
  GND: Part11.GND, SONAR1.GND
  N1: Part11.VBAT, SONAR1.+5V
  N2: Part11.D6, SONAR1.RX
  N3: Part11.D5, SONAR1.PW

custom parts:
  Adafruit Feather M0 Basic Proto: At the Feather M0's heart is an ATSAMD21G18 ARM Cortex M0 processor, clocked at 48 MHz and at 3.3V logic, the same one used in the new Arduino Zero. This chip has a whopping 256K of FLASH (8x more than the Atmega328 or 32u4) and 32K of RAM (16x as much)! This chip comes with built in USB so it has USB-to-Serial program & debug capability built in with no need for an FTDI-like chip. To make it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
  Maxbotix MaxSonar Ultrasonic Sensor (Hi-Res): Maxbotix MaxSonar Hi-Resolution Ultrasonic Sensor HRLV-EZ0, HRLV-EZ1, HRLV-EZ2, HRLV-EZ3, HRLV-EZ4
